// Logisim project lab4_milestone1.circ as structural Verilog: 4 circuits, main circuit ImmGen
module ImmGen (
  input  [31:0] Instruction,
  output [31:0] IMM32
);

  assign IMM32[31:12] = {{19{Instruction[31]}}, Instruction[31]};  // Bit_Extender bit_extender_1
  Multiplexer #(.enable("false"), .select(2)) multiplexer_1 (
    .in0(Instruction[20]), .in1(Instruction[7]), .in3(1'b0), .out(IMM32[0]), .sel(Instruction[6:5]));  // open: in2
  Multiplexer #(.enable("false"), .width(4)) multiplexer_2 (
    .in0(Instruction[24:21]), .in1(Instruction[11:8]), .out(IMM32[4:1]), .sel(Instruction[5]));
  Multiplexer #(.enable("false")) multiplexer_3 (
    .in0(Instruction[31]), .in1(Instruction[7]), .out(IMM32[11]), .sel(Instruction[6]));

  assign IMM32[10:5] = Instruction[30:25];

  // Other names for the same wires on the sheet: I30_25[5:0] = Instruction[30:25]; I5 = Instruction[5];
  //   I6_5[1:0] = Instruction[6:5]; I6 = Instruction[6]; I7 = Instruction[7]; I11_8[3:0] = Instruction[11:8];
  //   I_20 = Instruction[20]; I24_21[3:0] = Instruction[24:21]; I31 = Instruction[31]
endmodule

module ALU_Control (
  input  I6,
  input  I5,
  input  I4,
  input  I3,
  input  I2,
  input  I1,
  input  I0,
  output MemtoReg,
  output RegWrite,
  output MemRead,
  output MemWrite,
  output Branch
);

  wire not_1_out, not_2_out;

  not not_1 (not_1_out, I6);
  not not_2 (not_2_out, I5);
  not not_3 (MemtoReg, I4);
  or or_1 (RegWrite, not_2_out, I4);
  and and_1 (MemRead, not_2_out, MemtoReg);
  and and_2 (MemWrite, not_1_out, I5, MemtoReg);

  assign Branch = I6;
endmodule

module instructionMemory (
  input  [23:0] Adress,
  input  Clock_in,
  output [31:0] instruction
);

  wire not_1_out;

  not not_1 (not_1_out, Clock_in);
  RAM #(.addrWidth(22), .asyncread("true"), .dataWidth(32)) ram_1 (
    .addr(Adress[23:2]), .we(1'b0), .oe(not_1_out), .dout(instruction));  // open: clk, din
endmodule

module DataMemory (
  input  [25:0] Address,
  input  MemWrite,
  input  MemRead,
  input  Clock_in,
  input  [31:0] WriteData,
  output [31:0] instruction
);

  RAM #(.addrWidth(24), .dataWidth(32)) ram_1 (
    .addr(Address[25:2]), .we(MemWrite), .oe(MemRead), .clk(Clock_in), .din(WriteData), .dout(instruction));
endmodule
