// Logisim project name.circ as structural Verilog
module full_adder (
  input  A,
  input  B,
  input  C_in,
  output S,
  output C_out
);

  wire and_1_out, and_2_out, xor_1_out;

  xor xor_1 (xor_1_out, A, B);
  xor xor_2 (S, xor_1_out, C_in);
  and and_1 (and_1_out, xor_1_out, C_in);
  and and_2 (and_2_out, B, A);
  or or_1 (C_out, and_1_out, and_2_out);
endmodule

module ALU_Control (
  input  I30,
  input  I14,
  input  I13,
  input  I12,
  input  I6,
  input  I5,
  input  I4,
  output ALU_Src,
  output ALU_Ctrl3,
  output ALU_Ctrl2,
  output ALU_Ctrl1,
  output ALU_Ctrl0
);

  wire and_2_out, not_1_out, not_2_out, not_3_out, not_4_out, not_5_out;

  not not_1 (not_1_out, I14);
  not not_2 (not_2_out, I13);
  not not_3 (not_3_out, I12);
  not not_4 (not_4_out, I5);
  not not_5 (not_5_out, I4);
  or or_1 (ALU_Src, not_4_out, not_5_out);
  and and_1 (ALU_Ctrl2, I30, not_2_out, I5);
  or or_2 (ALU_Ctrl1, not_2_out, not_5_out);
  and and_2 (and_2_out, I13, not_3_out);
  or or_3 (ALU_Ctrl0, not_1_out, and_2_out);

  assign ALU_Ctrl3 = 1'b0;
endmodule

module oneBit_ALU (
  input  ALU_Ctrl,
  input  A,
  input  B,
  input  C_in,
  output R,
  output C_out
);

  wire and_1_out, full_adder_1_s, multiplexer_1_out, not_1_out, or_1_out, xor_1_out;
  wire [1:0] undriven;

  Multiplexer #(.enable("false")) multiplexer_1 (.in0(B), .in1(not_1_out), .out(multiplexer_1_out), .sel(ALU_Ctrl));
  not not_1 (not_1_out, B);
  and and_1 (and_1_out, A, multiplexer_1_out);
  or or_1 (or_1_out, A, multiplexer_1_out);
  xor xor_1 (xor_1_out, A, multiplexer_1_out);
  full_adder full_adder_1 (.A(A), .B(multiplexer_1_out), .C_in(C_in), .S(full_adder_1_s), .C_out(C_out));
  Multiplexer #(.enable("false"), .select(2)) multiplexer_2 (
    .in0(and_1_out), .in1(or_1_out), .in2(xor_1_out), .in3(full_adder_1_s), .out(R), .sel(undriven));
endmodule

module fourBit_ALU (
  input  [3:0] ALU_Ctrl,
  input  C_in,
  input  [3:0] A,
  input  [3:0] B,
  output [3:0] R,
  output C_out
);

  wire onebit_alu_1_c_out, onebit_alu_2_c_out, onebit_alu_3_c_out;

  oneBit_ALU onebit_alu_1 (.A(A[0]), .B(B[0]), .C_in(C_in), .R(R[0]), .C_out(onebit_alu_1_c_out));  // open: ALU_Ctrl
  oneBit_ALU onebit_alu_2 (
    .A(A[1]), .B(B[1]), .C_in(onebit_alu_1_c_out), .R(R[1]), .C_out(onebit_alu_2_c_out));  // open: ALU_Ctrl
  oneBit_ALU onebit_alu_3 (
    .A(A[2]), .B(B[2]), .C_in(onebit_alu_2_c_out), .R(R[2]), .C_out(onebit_alu_3_c_out));  // open: ALU_Ctrl
  oneBit_ALU onebit_alu_4 (.A(A[3]), .B(B[3]), .C_in(onebit_alu_3_c_out), .R(R[3]), .C_out(C_out));  // open: ALU_Ctrl
endmodule
